# Fritzing sketch GpioConsoleHost (saved by Fritzing 0.9.3b)
breadboards: 1

parts:
  Raspberry_Pi2 = Raspberry Pi B+
  LED1 = LED - 5mm [color="Red (633nm)" package="5 mm [THT]"]
  R2 = Resistor [tolerance=±5% resistance=470 package=THT]  # not connected
  J2 = Piezo Speaker
  LED2 = RGB LED (com. cathode, rgb) [package="5 mm [THT]"]
  R3 = Resistor [tolerance=±5% resistance=470 package=THT]
  R4 = Resistor [tolerance=±5% resistance=470 package=THT]
  R5 = Resistor [tolerance=±5% resistance=470 package=THT]
  Part1 = Breadboard Power Supply Board SMD
  J3 = Basic Servo
  Part2 = 16-Channel 12-bit PWM Servo Driver - I2C [part_number=815]
  Part3 = Digital Temperature Sensor Breakout - TMP102
  Part4 = Digital Temperature Sensor Breakout - TMP102  # not connected

nets:
  3V3: Raspberry_Pi2.3v3, Part2.VCC, Part3.V+
  N1: Raspberry_Pi2.GPIO2, Part2.SDA, Part3.SDA
  N2: Raspberry_Pi2.GPIO3, Part2.SCL, Part3.SCL
  GND: Raspberry_Pi2.GND, J2.pin1, Part1.GND, J3.gnd, Part2.GND, Part3.GND, Part3.ADD0
  N3: Raspberry_Pi2.GPIO17, R3.Pin_1
  N4: Raspberry_Pi2.GPIO27, R5.Pin_1
  N5: Raspberry_Pi2.GPIO16, J2.pin2
  N6: Raspberry_Pi2.GPIO23, LED1.anode
  N7: Raspberry_Pi2.GPIO18, R4.Pin_1
  N8: LED2.red_anode, R3.Pin_0
  N9: LED2.green_anode, R4.Pin_0
  N10: LED2.blue_anode, R5.Pin_0
  N11: Part1.VCC, Part2.PWRIN
  N12: J3.vcc, Part2.5.0V
  N13: J3.pulse, Part2.PWM0

notes:
  Tower Pro SG90 Servo
  External 5V power supply
  PCA9685 16 Channel 12 Bit PWM Servo Driver
  The new TMP102 model, SEN-11931, is used in the actual jpg images. The TMP102 here works, but is just an earlier version.

custom parts:
  16-Channel 12-bit PWM Servo Driver - I2C: You want to make a cool robot, maybe a hexapod walker, or maybe just a piece of art with a lot of moving parts. Or maybe you want to drive a lot of LEDs with precise PWM output. Using only two pins, control 16 free-running PWM outputs! You can even chain up 62 breakouts to control up to 992 PWM outputs.
